# Fritzing sketch Schema (saved by Fritzing 0.9.5d)
breadboards: 2

parts:
  Компонент1 = Arduino Uno (Rev3)  # not connected
  Компонент2 = InvenSense MPU6050
  U2 = GS406SMD [package=gs406smd]
  HC-SR04_Sensor_1 = HC-SR04 Ultrasonic Distance Sensor
  Компонент4 = Arduino Motor Shield (Rev3)
  U5 = FS1000A [package=THT]
  U6 = XD-RF-5V [package=THT]
  M1 = DC Motor
  VCC4 = Battery block 9V
  M2 = DC Motor
  M3 = Dagu DGServo 9g (End View) [part_number=RS001B]
  M4 = RioRand LM2596

nets:
  VCC: Компонент2.VCC, U2.P1, HC-SR04_Sensor_1.VCC, U5.DATA, U6.VCC, M3.vcc, M4.Pin_3
  GND: Компонент2.GND, U2.P5, HC-SR04_Sensor_1.GND, U5.GND, U6.GND, M3.gnd, M4.Pin_4
  N1: Компонент2.SCL, Компонент4.A5
  N2: Компонент2.SDA, Компонент4.A4
  N3: HC-SR04_Sensor_1.TRIG, Компонент4.D10_PWM
  N4: HC-SR04_Sensor_1.ECHO, Компонент4.D11_PWM/B
  N5: Компонент4.D9/BreakeA, M3.pulse
  N6: Компонент4.D12/DirA, U5.VCC
  N7: Компонент4.D13/DirB, U6.DATA
  N8: Компонент4.B-, M1.pin_2
  N9: Компонент4.B+, M1.pin_1
  N10: Компонент4.A-, M2.pin_2
  N11: Компонент4.A+, M2.pin_1
  N12: Компонент4.VMOT, VCC4.+, M4.Pin_1
  N13: Компонент4.GND, VCC4.-, M4.Pin_2

notes:
  1) Щеточный мотор с двумя проводами (2): подключение к выходам M1 и M2 на Arduino Motor Shield.
  2) Servo (1): подключение сигнального пина к выходу D9 на Arduino Uno.
  3) Ultrasonic distance sensor HC-SR04 (1): подключение пина Trig к выходу D10, пина Echo к выходу D11, питание к 5V, и GND к GND.
  4) Transmitter FS1000 (1): подключение пина Data к выходу D12, питание к 5V, и GND к GND.
  5) Receiver MX-RM-5V (1): подключение пина Data к выходу D13, питание к 5V, и GND к GND.
  6) MPU6050 (1): подключение SDA к A4, SCL к A5, питание к 5V, и GND к GND.
  7) Trema GPS ATGM336H и GPS антенна (1): подключение TX к выходу D7, RX к выходу D8, питание к 5V, и GND к GND.
  1) Щеточные моторы с двумя проводами (2): Обычно, на каждый мотор требуется напряжение в диапазоне от 6V до 12V. Для каждого мотора вы можете посмотреть его характеристики на документации или на самом моторе, чтобы узнать его потребляемую мощность в ваттах (W).
  2) Сервопривод (1): Сервоприводы обычно потребляют напряжение в диапазоне от 4,8V до 6V. Опять же, для вашего конкретного сервопривода вы можете посмотреть его характеристики для определения потребляемой мощности.
  3) Ультразвуковой датчик расстояния HC-SR04 (1): Датчик работает с напряжением 5V.
  4) Передатчик FS1000 (1): Работает с напряжением 5V.
  5) Приемник MX-RM-5V (1): Работает с напряжением 5V.
  6) MPU6050 (1): Работает с напряжением 5V.
  7) Трекинговый приемник GPS ATGM336H и антенна (1): Оба устройства работают с напряжением 5V.
  8) Arduino Motor Shield: Шилд может быть питаем напрямую от аккумулятора, но потребляет энергию при работе моторов и других устройств.

custom parts:
  FS1000A: This is 433Mhz RF transmitter with receiver kit for Arduino ARM MCU wireless Application environment: Remote control switch, receiver module, motorcycles, automobile anti-theft products, home security products, electric doors, shutter doors, windows, remote control socket, remote control LED, remote audio remote control electric doors, garage door remote control, remote control retractable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
  XD-RF-5V: This is 433Mhz RF transmitter with receiver kit for Arduino ARM MCU wireless Application environment: Remote control switch, receiver module, motorcycles, automobile anti-theft products, home security products, electric doors, shutter doors, windows, remote control socket, remote control LED, remote audio remote control electric doors, garage door remote control, remote control retractable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
